// Digital circuit address-register-control-input.dig as structural Verilog
module address_register_control_input (
  input  LOAD,
  input  CE,
  input  RST,
  input  J2,
  input  J3,
  input  [1:0] B,
  input  B2,
  input  B3,
  output CE0,
  output CE1,
  output CE2,
  output CE3,
  output LD0,
  output LD1,
  output LD2,
  output LD3,
  output BBS
);

  wire CS0, CS1, CS2, CS3, decoder_1_out_0, decoder_1_out_1, decoder_1_out_2, decoder_1_out_3, not_1_out,
       not_2_out, not_3_out, not_4_out, or_10_out, or_11_out, or_12_out, or_13_out, xor_1_out, xor_2_out;

  xor xor_1 (xor_1_out, B3, J3);
  xor xor_2 (xor_2_out, B2, J2);
  Decoder #(.Selector_Bits(2)) decoder_1 (
    .sel(B), .out_0(decoder_1_out_0), .out_1(decoder_1_out_1), .out_2(decoder_1_out_2),
    .out_3(decoder_1_out_3));
  or or_1 (BBS, xor_1_out, xor_2_out);
  not not_1 (not_1_out, decoder_1_out_0);
  not not_2 (not_2_out, decoder_1_out_1);
  not not_3 (not_3_out, decoder_1_out_2);
  not not_4 (not_4_out, decoder_1_out_3);
  or or_2 (CS0, BBS, not_1_out);
  or or_3 (CS1, BBS, not_2_out);
  or or_4 (CS2, not_3_out, BBS);
  or or_5 (CS3, not_4_out, BBS);
  or or_6 (CE0, CS0, CE);
  or or_7 (CE1, CS1, CE);
  or or_8 (CE2, CS2, CE);
  or or_9 (CE3, CS3, CE);
  or or_10 (or_10_out, CS0, LOAD);
  or or_11 (or_11_out, CS1, LOAD);
  or or_12 (or_12_out, CS2, LOAD);
  or or_13 (or_13_out, CS3, LOAD);
  and and_1 (LD0, or_10_out, RST);
  and and_2 (LD1, or_11_out, RST);
  and and_3 (LD2, or_12_out, RST);
  and and_4 (LD3, or_13_out, RST);

  // Notes on the sheet:
  //   LOAD: pin 9
  //   CE: pin 8
  //   RST: pin 10
  //   J2: pin 5
  //   J3: pin 3
  //   CE0: pin 15
  //   CE1: pin 16
  //   CE2: pin 17
  //   CE3: pin 18
  //   B: pin 7,6
  //   LD0: pin 19
  //   LD1: pin 20
  //   LD2: pin 21
  //   LD3: pin 22
  //   B2: pin 4
  //   B3: pin 2
  //   BBS: pin 14
endmodule
