// Digital circuit 74LS243.dig as structural Verilog
module _74LS243 (
  input  GBA,
  input  nGAB,
  input  A0,
  input  A1,
  input  A2,
  input  A3,
  output B3,
  output B2,
  output B1,
  output B0
);

  assign B3 = ~nGAB ? A3 : 1'bz;  // DriverInvSel driverinvsel_1
  assign B2 = ~nGAB ? A2 : 1'bz;  // DriverInvSel driverinvsel_2
  assign B1 = ~nGAB ? A1 : 1'bz;  // DriverInvSel driverinvsel_3
  assign B0 = ~nGAB ? A0 : 1'bz;  // DriverInvSel driverinvsel_4
  assign A3 = GBA ? B3 : 1'bz;  // Driver driver_1
  assign A2 = GBA ? B2 : 1'bz;  // Driver driver_2
  assign A1 = GBA ? B1 : 1'bz;  // Driver driver_3
  assign A0 = GBA ? B0 : 1'bz;  // Driver driver_4

  // Notes on the sheet:
  //   nGAB: default 1
endmodule
