// Digital circuit 74LS379.dig as structural Verilog
module _74LS379 (
  input  D3,
  input  D2,
  input  D1,
  input  D0,
  input  nG,
  input  CLK,
  output Q3,
  output Q2,
  output Q1,
  output Q0,
  output nQ3,
  output nQ2,
  output nQ1,
  output nQ0
);

  wire or_1_out;

  or or_1 (or_1_out, nG, CLK);
  D_FF d_ff_1 (.D(D3), .C(or_1_out), .Q(Q3), .nQ(nQ3));
  D_FF d_ff_2 (.D(D2), .C(or_1_out), .Q(Q2), .nQ(nQ2));
  D_FF d_ff_3 (.D(D1), .C(or_1_out), .Q(Q1), .nQ(nQ1));
  D_FF d_ff_4 (.D(D0), .C(or_1_out), .Q(Q0), .nQ(nQ0));
endmodule
