// Digital circuit alu-design.dig as structural Verilog
module alu_design (
  input  D3,
  input  D2,
  input  D1,
  input  D0,
  input  nLDB,
  input  CLK,
  input  nLDA,
  input  IE,
  input  nLDF,
  input  nOE,
  input  S3,
  input  S2,
  input  S1,
  input  S0,
  input  nCLF,
  output A3,
  output A2,
  output A1,
  output A0,
  output B3,
  output B2,
  output B1,
  output B0,
  output D0_2,
  output D1_2,
  output D2_2,
  output D3_2,
  output CF,
  output ZF,
  output OVR,
  output EQ,
  output LT,
  output GT,
  output nSUB,
  output nCE,
  output nNOT,
  output nNEG,
  output nCMP,
  output nF382,
  output O2,
  output O1,
  output O0
);

  wire _74173_2_pin15, _74382_1_pin8, _74382_1_pin9, _74382_1_pin11, _74382_1_pin12, _74382_1_pin13,
       _74382_1_pin14, and_1_out, and_2_out, cin, cmpe, cmpg, cmpl, cout, f0, f1, f2, f3, nA0, nA1, nA2, nA3,
       nadd, nand_1_out, nand_2_out, nand_3_out, not_1_out, not_3_out, not_4_out, not_5_out, not_6_out,
       or_2_out, or_3_out, or_4_out, ovr_t, Y0, Y1, Y2, Y3, zero;

  nand nand_1 (nand_1_out, nSUB, nCMP);
  not not_1 (not_1_out, nCE);
  _74157 _74157_1 (
    .pin1(nNEG), .pin2(1'b0), .pin3(B0), .pin4(Y0), .pin5(1'b0), .pin6(B1), .pin7(Y1), .pin8(1'b0),
    .pin9(Y2), .pin10(B2), .pin11(1'b0), .pin12(Y3), .pin13(B3), .pin14(1'b0), .pin15(1'b0), .pin16(1'b1));
  and and_1 (and_1_out, not_1_out, CF);
  and and_2 (and_2_out, nCE, nand_1_out);
  or or_1 (cin, and_1_out, and_2_out);
  decoder decoder_1 (
    .S3(S3), .S2(S2), .S1(S1), .S0(S0), .F0(O0), .F1(O1), .F2(O2), .nNEGA(nNEG), .nNOTA(nNOT), .nF382(nF382),
    .nCMP(nCMP), .nCE(nCE), .nADD(nadd), .nSUB(nSUB));
  assign D3_2 = IE ? D3 : 1'bz;  // Driver driver_1
  _74382 _74382_1 (
    .pin1(A1), .pin2(Y1), .pin3(A0), .pin4(Y0), .pin5(O0), .pin6(O1), .pin7(O2), .pin8(_74382_1_pin8),
    .pin9(_74382_1_pin9), .pin10(1'b0), .pin11(_74382_1_pin11), .pin12(_74382_1_pin12),
    .pin13(_74382_1_pin13), .pin14(_74382_1_pin14), .pin15(cin), .pin16(Y3), .pin17(A3), .pin18(Y2),
    .pin19(A2), .pin20(1'b1));
  assign D2_2 = IE ? D2 : 1'bz;  // Driver driver_2
  assign D1_2 = IE ? D1 : 1'bz;  // Driver driver_3
  assign D0_2 = IE ? D0 : 1'bz;  // Driver driver_4
  _74LS243 _74ls243_1 (
    .GBA(1'b0), .nGAB(nF382), .A0(_74382_1_pin8), .A1(_74382_1_pin9), .A2(_74382_1_pin11),
    .A3(_74382_1_pin12), .B3(f3), .B2(f2), .B1(f1), .B0(f0));
  nand nand_2 (nand_2_out, nadd, nSUB);
  _74LS379 _74ls379_1 (
    .D3(D3_2), .D2(D2_2), .D1(D1_2), .D0(D0_2), .nG(nLDA), .CLK(CLK), .Q3(A3), .Q2(A2), .Q1(A1), .Q0(A0),
    .nQ3(nA3), .nQ2(nA2), .nQ1(nA1), .nQ0(nA0));
  _74LS243 _74ls243_2 (
    .GBA(1'b0), .nGAB(nNOT), .A0(nA0), .A1(nA1), .A2(nA2), .A3(nA3), .B3(f3), .B2(f2), .B1(f1), .B0(f0));
  _74173 _74173_1 (
    .pin1(1'b0), .pin2(1'b0), .pin3(B0), .pin4(B1), .pin5(B2), .pin6(B3), .pin7(CLK), .pin8(1'b0),
    .pin9(nLDB), .pin10(nLDB), .pin11(D3_2), .pin12(D2_2), .pin13(D1_2), .pin14(D0_2), .pin15(1'b0),
    .pin16(1'b1));
  and and_3 (cout, _74382_1_pin14, nand_2_out);
  and and_4 (ovr_t, nand_2_out, _74382_1_pin13);
  or or_2 (or_2_out, f0, f1);
  or or_3 (or_3_out, f2, f3);
  or or_4 (or_4_out, or_2_out, or_3_out);
  not not_2 (zero, or_4_out);
  not not_3 (not_3_out, nCLF);
  _74173 _74173_2 (
    .pin1(1'b0), .pin2(1'b0), .pin3(CF), .pin4(OVR), .pin7(CLK), .pin8(1'b0), .pin9(nLDF), .pin10(nLDF),
    .pin11(1'b0), .pin12(1'b0), .pin13(ovr_t), .pin14(cout), .pin15(_74173_2_pin15), .pin16(1'b1));  // open: pin5, pin6
  and and_5 (_74173_2_pin15, CLK, not_3_out);
  nand nand_3 (nand_3_out, or_4_out, _74382_1_pin14);
  not not_4 (not_4_out, _74382_1_pin14);
  _74173 _74173_3 (
    .pin1(1'b0), .pin2(1'b0), .pin3(ZF), .pin4(EQ), .pin5(LT), .pin6(GT), .pin7(CLK), .pin8(1'b0),
    .pin9(nLDF), .pin10(nLDF), .pin11(cmpg), .pin12(cmpl), .pin13(cmpe), .pin14(zero),
    .pin15(_74173_2_pin15), .pin16(1'b1));
  not not_5 (not_5_out, nCMP);
  not not_6 (not_6_out, nand_3_out);
  and and_6 (cmpl, not_5_out, not_4_out);
  and and_7 (cmpe, not_5_out, zero);
  and and_8 (cmpg, not_5_out, not_6_out);
  _74LS243 _74ls243_3 (
    .GBA(1'b0), .nGAB(nOE), .A0(f0), .A1(f1), .A2(f2), .A3(f3), .B3(D3_2), .B2(D2_2), .B1(D1_2), .B0(D0_2));

  // Other names for the same wires on the sheet: D0_t = D0_2; D1_t = D1_2; D2_t = D2_2; D3_t = D3_2; nclrf = nCLF;
  //   nnega = nNEG; nnota = nNOT; of = OVR

  // Notes on the sheet:
  //   nLDB: default 1
  //   nLDA: default 1
  //   nLDF: default 1
  //   nOE: default 1
  //   nCLF: default 1
endmodule
