// Digital circuit decoder2.dig as structural Verilog
// 22V10B GAL Decoder
module decoder2 (
  input  S3,
  input  S2,
  input  S1,
  input  S0,
  output F0,
  output F1,
  output F2,
  output nNEGA,
  output nNOTA,
  output nF382,
  output nCMP,
  output nCE,
  output nADD,
  output nSUB
);

  wire ADD_out, SUB_out;

  LookUpTable #(.Bits(3)) FSEL (.in0(S0), .in1(S1), .in2(S2), .in3(S3), .out({F2, F1, F0}));
  LookUpTable #(.Bits(4)) FSEL2 (.in0(S0), .in1(S1), .in2(S2), .in3(S3), .out({nCMP, nNOTA, nNEGA, nF382}));
  LookUpTable CARRY (.in0(S0), .in1(S1), .in2(S2), .in3(S3), .out(nCE));
  LookUpTable SUB (.in0(S0), .in1(S1), .in2(S2), .in3(S3), .out(SUB_out));
  LookUpTable ADD (.in0(S0), .in1(S1), .in2(S2), .in3(S3), .out(ADD_out));
  not not_1 (nSUB, SUB_out);
  not not_2 (nADD, ADD_out);

  // Notes on the sheet:
  //   S3: pin 5
  //   S2: pin 4
  //   S1: pin 3
  //   S0: pin 2
  //   F0: pin 14
  //   F1: pin 15
  //   F2: pin 16
  //   nNEGA: pin 22
  //   nNOTA: pin 23
  //   nF382: pin 17
  //   nCMP: pin 20
  //   nCE: pin 21
  //   nADD: pin 19
  //   nSUB: pin 18
  //   contents of FSEL (hex, n*v repeats v):
  //   3,3,2,2,1,0,5,6,4,0,0,0,2
  //   contents of FSEL2 (hex, n*v repeats v):
  //   e,e,e,e,c,f,e,e,e,b,f,f,6,f,f,f
  //   contents of CARRY (hex, n*v repeats v):
  //   1,0,1,0,1,1,1,1,1,1,1,1,1,1,1,1
  //   contents of SUB (hex, n*v repeats v):
  //   0,0,1,1,1
  //   contents of ADD (hex, n*v repeats v):
  //   1,1,a,a,a
endmodule
