// Digital circuit alu-design.dig as structural Verilog
module alu_design (
  input  D3,
  input  D2,
  input  D1,
  input  D0,
  input  nLDB,
  input  CLK,
  input  nLDA,
  input  IE,
  input  nLDF,
  input  nOE,
  input  S3,
  input  S2,
  input  S1,
  input  S0,
  input  nEN,
  output A3,
  output A2,
  output A1,
  output A0,
  output B3,
  output B2,
  output B1,
  output B0,
  output D0_2,
  output D1_2,
  output D2_2,
  output D3_2,
  output CF,
  output ZF,
  output OVR,
  output EQ,
  output LT,
  output GT,
  output nADD,
  output nSUB,
  output nCE,
  output nNOT,
  output nNEG,
  output nCMP,
  output nOR,
  output nAND,
  output nXOR,
  output nCLRF
);

  wire _7485_1_pin5, _7485_1_pin6, _7485_1_pin7, _74157_1_pin4, _74157_1_pin7, _74157_1_pin9, _74157_1_pin12,
       _74173_1_pin15, _74283_1_pin1, _74283_1_pin4, _74283_1_pin10, _74283_1_pin13, _74283_2_pin9,
       and_4_out, and_5_out, and_6_out, and_7_out, and_8_out, and_9_out, cin, cmpe, cmpg, cmpl, cout, f0, f1,
       f2, f3, nA0, nA1, nA2, nA3, nand_1_out, nand_2_out, nand_3_out, nand_4_out, nB0, nB1, nB2, nB3,
       not_1_out, not_2_out, not_3_out, not_4_out, not_5_out, nsadd, nsaddc, nssub, nssubc, or_1_out,
       or_2_out, or_3_out, or_4_out, or_5_out, ovr_t, S0_t, S1_t, S2_t, S3_t, xor_2_out, xor_3_out,
       xor_4_out, xor_5_out, xor_6_out, xor_7_out, zero;

  _74154 _74154_1 (
    .pin1(nsadd), .pin2(nsaddc), .pin3(nssub), .pin4(nssubc), .pin5(nNEG), .pin7(nOR), .pin8(nAND),
    .pin9(nXOR), .pin10(nNOT), .pin12(1'b0), .pin14(nCMP), .pin17(nCLRF), .pin18(nEN), .pin19(nEN),
    .pin20(S3), .pin21(S2), .pin22(S1), .pin23(S0), .pin24(1'b1));  // open: pin6, pin11, pin13, pin15, pin16
  and and_1 (nADD, nsadd, nsaddc);
  and and_2 (nSUB, nssub, nssubc);
  and and_3 (nCE, nsaddc, nssubc);
  assign D3_2 = IE ? D3 : 1'bz;  // Driver driver_1
  _74283 _74283_1 (
    .pin1(_74283_1_pin1), .pin2(nA1), .pin3(1'b0), .pin4(_74283_1_pin4), .pin5(1'b0), .pin6(nA0),
    .pin7(1'b1), .pin8(1'b0), .pin10(_74283_1_pin10), .pin11(nA3), .pin12(1'b0), .pin13(_74283_1_pin13),
    .pin14(1'b0), .pin15(nA2), .pin16(1'b1));  // open: pin9
  or or_1 (or_1_out, A0, B0);
  or or_2 (or_2_out, A1, B1);
  or or_3 (or_3_out, A2, B2);
  or or_4 (or_4_out, A3, B3);
  assign D2_2 = IE ? D2 : 1'bz;  // Driver driver_2
  assign D1_2 = IE ? D1 : 1'bz;  // Driver driver_3
  _74157 _74157_1 (
    .pin1(nADD), .pin2(B0), .pin3(nB0), .pin4(_74157_1_pin4), .pin5(B1), .pin6(nB1), .pin7(_74157_1_pin7),
    .pin8(1'b0), .pin9(_74157_1_pin9), .pin10(nB2), .pin11(B2), .pin12(_74157_1_pin12), .pin13(nB3),
    .pin14(B3), .pin15(1'b0), .pin16(1'b1));
  not not_1 (not_1_out, nCE);
  not not_2 (not_2_out, nSUB);
  assign D0_2 = IE ? D0 : 1'bz;  // Driver driver_4
  and and_4 (and_4_out, not_1_out, CF);
  _74LS243 _74ls243_1 (
    .GBA(1'b0), .nGAB(nOR), .A0(or_1_out), .A1(or_2_out), .A2(or_3_out), .A3(or_4_out), .B3(f3), .B2(f2),
    .B1(f1), .B0(f0));
  or or_5 (or_5_out, and_4_out, not_1_out);
  _74LS379 _74ls379_1 (
    .D3(D3_2), .D2(D2_2), .D1(D1_2), .D0(D0_2), .nG(nLDA), .CLK(CLK), .Q3(A3), .Q2(A2), .Q1(A1), .Q0(A0),
    .nQ3(nA3), .nQ2(nA2), .nQ1(nA1), .nQ0(nA0));
  _74LS379 _74ls379_2 (
    .D3(D3_2), .D2(D2_2), .D1(D1_2), .D0(D0_2), .nG(nLDB), .CLK(CLK), .Q3(B3), .Q2(B2), .Q1(B1), .Q0(B0),
    .nQ3(nB3), .nQ2(nB2), .nQ1(nB1), .nQ0(nB0));
  _74LS243 _74ls243_2 (
    .GBA(1'b0), .nGAB(nNOT), .A0(nA0), .A1(nA1), .A2(nA2), .A3(nA3), .B3(f3), .B2(f2), .B1(f1), .B0(f0));
  _74LS243 _74ls243_3 (
    .GBA(1'b0), .nGAB(nNEG), .A0(_74283_1_pin4), .A1(_74283_1_pin1), .A2(_74283_1_pin13),
    .A3(_74283_1_pin10), .B3(f3), .B2(f2), .B1(f1), .B0(f0));
  _74283 _74283_2 (
    .pin1(S1_t), .pin2(_74157_1_pin7), .pin3(A1), .pin4(S0_t), .pin5(A0), .pin6(_74157_1_pin4), .pin7(cin),
    .pin8(1'b0), .pin9(_74283_2_pin9), .pin10(S3_t), .pin11(_74157_1_pin12), .pin12(A3), .pin13(S2_t),
    .pin14(A2), .pin15(_74157_1_pin9), .pin16(1'b1));
  xor xor_1 (cin, or_5_out, not_2_out);
  and and_5 (and_5_out, A0, B0);
  and and_6 (and_6_out, A1, B1);
  and and_7 (and_7_out, A2, B2);
  and and_8 (and_8_out, A3, B3);
  xor xor_2 (xor_2_out, S3_t, _74283_2_pin9);
  xor xor_3 (xor_3_out, _74283_2_pin9, not_2_out);
  and and_9 (and_9_out, nADD, nSUB);
  _74LS243 _74ls243_4 (
    .GBA(1'b0), .nGAB(nAND), .A0(and_5_out), .A1(and_6_out), .A2(and_7_out), .A3(and_8_out), .B3(f3),
    .B2(f2), .B1(f1), .B0(f0));
  _7485 _7485_1 (
    .pin1(B3), .pin2(1'b0), .pin3(1'b1), .pin4(1'b0), .pin5(_7485_1_pin5), .pin6(_7485_1_pin6),
    .pin7(_7485_1_pin7), .pin8(1'b0), .pin9(B0), .pin10(A0), .pin11(B1), .pin12(A1), .pin13(A2), .pin14(B2),
    .pin15(A3), .pin16(1'b1));
  not not_3 (not_3_out, and_9_out);
  nand nand_1 (nand_1_out, f0, f1);
  nand nand_2 (nand_2_out, f2, f3);
  and and_10 (ovr_t, xor_2_out, not_3_out);
  and and_11 (cout, not_3_out, xor_3_out);
  not not_4 (not_4_out, nCLRF);
  _74173 _74173_1 (
    .pin1(1'b0), .pin2(1'b0), .pin3(CF), .pin4(OVR), .pin7(CLK), .pin8(1'b0), .pin9(nLDF), .pin10(nLDF),
    .pin11(1'b0), .pin12(1'b0), .pin13(ovr_t), .pin14(cout), .pin15(_74173_1_pin15), .pin16(1'b1));  // open: pin5, pin6
  _74LS243 _74ls243_5 (
    .GBA(1'b0), .nGAB(and_9_out), .A0(S0_t), .A1(S1_t), .A2(S2_t), .A3(S3_t), .B3(f3), .B2(f2), .B1(f1),
    .B0(f0));
  nand nand_3 (nand_3_out, nand_1_out, nand_2_out);
  xor xor_4 (xor_4_out, A0, B0);
  xor xor_5 (xor_5_out, A1, B1);
  xor xor_6 (xor_6_out, A2, B2);
  xor xor_7 (xor_7_out, A3, B3);
  and and_12 (_74173_1_pin15, CLK, not_4_out);
  not not_5 (not_5_out, nCMP);
  nand nand_4 (nand_4_out, nand_3_out, nand_3_out);
  _74173 _74173_2 (
    .pin1(1'b0), .pin2(1'b0), .pin3(ZF), .pin4(EQ), .pin5(LT), .pin6(GT), .pin7(CLK), .pin8(1'b0),
    .pin9(nLDF), .pin10(nLDF), .pin11(cmpg), .pin12(cmpl), .pin13(cmpe), .pin14(zero),
    .pin15(_74173_1_pin15), .pin16(1'b1));
  and and_13 (cmpl, not_5_out, _7485_1_pin7);
  and and_14 (cmpe, not_5_out, _7485_1_pin6);
  and and_15 (cmpg, not_5_out, _7485_1_pin5);
  _74LS243 _74ls243_6 (
    .GBA(1'b0), .nGAB(nOE), .A0(f0), .A1(f1), .A2(f2), .A3(f3), .B3(D3_2), .B2(D2_2), .B1(D1_2), .B0(D0_2));
  and and_16 (zero, nCMP, nand_4_out);
  _74LS243 _74ls243_7 (
    .GBA(1'b0), .nGAB(nXOR), .A0(xor_4_out), .A1(xor_5_out), .A2(xor_6_out), .A3(xor_7_out), .B3(f3),
    .B2(f2), .B1(f1), .B0(f0));

  // Other names for the same wires on the sheet: D0_t = D0_2; D1_t = D1_2; D2_t = D2_2; D3_t = D3_2; nnega = nNEG;
  //   nnota = nNOT; of = OVR

  // Notes on the sheet:
  //   nLDB: default 1
  //   nLDA: default 1
  //   nLDF: default 1
  //   nOE: default 1
  //   nEN: default 1
endmodule
