// Digital circuit alu-181-sim.dig as structural Verilog
module alu_181_sim (
  input  A3,
  input  A2,
  input  A1,
  input  A0,
  input  B3,
  input  B2,
  input  B1,
  input  B0,
  input  S3,
  input  S2,
  input  S1,
  input  S0,
  input  M,
  input  nCn,
  output F3,
  output F2,
  output F1,
  output F0,
  output nCn_plus_4,
  output P,
  output G,
  output A_eq_B
);

  _74181 _74181_1 (
    .pin1(B0), .pin2(A0), .pin3(S3), .pin4(S2), .pin5(S1), .pin6(S0), .pin7(nCn), .pin8(M), .pin9(F0),
    .pin10(F1), .pin11(F2), .pin12(1'b0));  // open: pin13, pin14, pin15, pin16, pin17, pin18, pin19, pin20, pin21, pin22, pin23, pin24
endmodule
