// Digital circuit alu-sim.dig as structural Verilog
module alu_sim (
  input  in_2,
  input  in_3,
  input  in_4,
  input  in_5,
  input  in_6,
  input  in_7,
  input  in_8,
  input  in_9,
  input  in_10,
  input  in_11,
  input  in_12,
  input  in_13,
  input  in_19,
  output out_1,
  output out_14,
  output out_15,
  output out_16,
  output out_17,
  output out_18
);

  wire _7404_1_pin2, _7404_1_pin4, _7404_1_pin6, _7404_1_pin8, _74382_1_pin8, _74382_1_pin9, _74382_1_pin11,
       _74382_1_pin12;

  _74382 _74382_1 (
    .pin1(in_4), .pin2(in_8), .pin3(in_5), .pin4(in_9), .pin5(in_12), .pin6(in_11), .pin7(in_10),
    .pin8(_74382_1_pin8), .pin9(_74382_1_pin9), .pin10(1'b0), .pin11(_74382_1_pin11), .pin12(_74382_1_pin12),
    .pin13(out_14), .pin14(out_1), .pin15(in_13), .pin16(in_6), .pin17(in_2), .pin18(in_7), .pin19(in_3),
    .pin20(1'b1));
  _7404 _7404_1 (
    .pin1(in_2), .pin2(_7404_1_pin2), .pin3(in_3), .pin4(_7404_1_pin4), .pin5(in_4), .pin6(_7404_1_pin6),
    .pin7(1'b0), .pin8(_7404_1_pin8), .pin9(in_5), .pin11(in_5), .pin13(in_5), .pin14(1'b1));  // open: pin10, pin12
  _74157 _74157_1 (
    .pin1(in_19), .pin2(_74382_1_pin8), .pin3(_7404_1_pin8), .pin4(out_18), .pin5(_74382_1_pin9),
    .pin6(_7404_1_pin6), .pin7(out_17), .pin8(1'b0), .pin9(out_16), .pin10(_7404_1_pin4),
    .pin11(_74382_1_pin11), .pin12(out_15), .pin13(_7404_1_pin2), .pin14(_74382_1_pin12), .pin15(1'b0),
    .pin16(1'b1));
endmodule
