// Digital circuit data-register-control-input.dig as structural Verilog
module data_register_control_input (
  input  B3,
  input  B2,
  input  J2,
  input  J3,
  input  [1:0] B,
  input  LD,
  input  RESET,
  output BBS,
  output LD0,
  output LD1,
  output LD2,
  output LD3,
  output RST
);

  wire decoder_1_out_0, decoder_1_out_1, decoder_1_out_2, decoder_1_out_3, not_1_out, not_2_out, not_3_out,
       not_4_out, xor_1_out, xor_2_out;

  xor xor_1 (xor_1_out, B3, J3);
  xor xor_2 (xor_2_out, B2, J2);
  Decoder #(.Selector_Bits(2)) decoder_1 (
    .sel(B), .out_0(decoder_1_out_0), .out_1(decoder_1_out_1), .out_2(decoder_1_out_2),
    .out_3(decoder_1_out_3));
  or or_1 (BBS, xor_1_out, xor_2_out);
  not not_1 (not_1_out, decoder_1_out_0);
  not not_2 (not_2_out, decoder_1_out_1);
  not not_3 (not_3_out, decoder_1_out_2);
  not not_4 (not_4_out, decoder_1_out_3);
  or or_2 (LD0, BBS, LD, not_1_out);
  or or_3 (LD1, BBS, LD, not_2_out);
  or or_4 (LD2, not_3_out, LD, BBS);
  or or_5 (LD3, not_4_out, LD, BBS);
  not not_5 (RST, RESET);

  // Notes on the sheet:
  //   B3: pin 2
  //   B2: pin 4
  //   J2: pin 5
  //   J3: pin 3
  //   BBS: pin 12
  //   B: pin 7,6
  //   LD: pin 8
  //   LD0: pin 13
  //   LD1: pin 14
  //   LD2: pin 15
  //   LD3: pin 16
  //   RST: pin 17
  //   RESET: pin 9
endmodule
