// Digital circuit data-register-control-output-patched.dig as structural Verilog
module data_register_control_output_patched (
  input  [1:0] A,
  input  OE,
  input  A3,
  input  A2,
  input  J2,
  input  J3,
  output OE0,
  output OE1,
  output OE2,
  output OE3,
  output ABS
);

  wire decoder_1_out_0, decoder_1_out_1, decoder_1_out_2, decoder_1_out_3, not_1_out, not_2_out, not_3_out,
       not_4_out, xor_1_out, xor_2_out;

  xor xor_1 (xor_1_out, A3, J3);
  xor xor_2 (xor_2_out, A2, J2);
  Decoder #(.Selector_Bits(2)) decoder_1 (
    .sel(A), .out_0(decoder_1_out_0), .out_1(decoder_1_out_1), .out_2(decoder_1_out_2),
    .out_3(decoder_1_out_3));
  or or_1 (ABS, xor_1_out, xor_2_out);
  not not_1 (not_1_out, decoder_1_out_0);
  not not_2 (not_2_out, decoder_1_out_1);
  not not_3 (not_3_out, decoder_1_out_2);
  not not_4 (not_4_out, decoder_1_out_3);
  nor nor_1 (OE0, ABS, OE, not_1_out);
  nor nor_2 (OE1, ABS, OE, not_2_out);
  nor nor_3 (OE2, not_3_out, OE, ABS);
  nor nor_4 (OE3, not_4_out, OE, ABS);

  // Notes on the sheet:
  //   A: pin 8,7
  //   OE: pin 9
  //   A3: pin 3
  //   A2: pin 5
  //   J2: pin 6
  //   J3: pin 4
  //   OE0: pin 13
  //   OE1: pin 14
  //   OE2: pin 15
  //   OE3: pin 16
  //   ABS: pin 12
endmodule
