// Digital circuit data-register-control.dig as structural Verilog
module data_register_control (
  input  [1:0] A,
  input  OE,
  input  A3,
  input  A2,
  input  J2,
  input  J3,
  input  [1:0] B,
  input  LD,
  output OE0,
  output OE1,
  output OE2,
  output OE3,
  output ABS,
  output LD0,
  output LD1,
  output LD2,
  output LD3
);

  wire decoder_1_out_0, decoder_1_out_1, decoder_1_out_2, decoder_1_out_3, decoder_2_out_0, decoder_2_out_1,
       decoder_2_out_2, decoder_2_out_3, not_1_out, not_2_out, not_3_out, not_4_out, not_5_out, not_6_out,
       not_7_out, not_8_out, xor_1_out, xor_2_out;

  xor xor_1 (xor_1_out, A3, J3);
  xor xor_2 (xor_2_out, A2, J2);
  Decoder #(.Selector_Bits(2)) decoder_1 (
    .sel(A), .out_0(decoder_1_out_0), .out_1(decoder_1_out_1), .out_2(decoder_1_out_2),
    .out_3(decoder_1_out_3));
  Decoder #(.Selector_Bits(2)) decoder_2 (
    .sel(B), .out_0(decoder_2_out_0), .out_1(decoder_2_out_1), .out_2(decoder_2_out_2),
    .out_3(decoder_2_out_3));
  or or_1 (ABS, xor_1_out, xor_2_out);
  not not_1 (not_1_out, decoder_1_out_0);
  not not_2 (not_2_out, decoder_1_out_1);
  not not_3 (not_3_out, decoder_1_out_2);
  not not_4 (not_4_out, decoder_1_out_3);
  not not_5 (not_5_out, decoder_2_out_0);
  not not_6 (not_6_out, decoder_2_out_1);
  not not_7 (not_7_out, decoder_2_out_2);
  not not_8 (not_8_out, decoder_2_out_3);
  or or_2 (OE0, ABS, OE, not_1_out);
  or or_3 (OE1, ABS, OE, not_2_out);
  or or_4 (OE2, not_3_out, OE, ABS);
  or or_5 (OE3, not_4_out, OE, ABS);
  or or_6 (LD0, ABS, LD, not_5_out);
  or or_7 (LD1, ABS, LD, not_6_out);
  or or_8 (LD2, not_7_out, LD, ABS);
  or or_9 (LD3, not_8_out, LD, ABS);

  // Notes on the sheet:
  //   A: pin 7,6
  //   OE: pin 8
  //   A3: pin 2
  //   A2: pin 4
  //   J2: pin 5
  //   J3: pin 3
  //   OE0: pin 15
  //   OE1: pin 16
  //   OE2: pin 17
  //   OE3: pin 18
  //   ABS: pin 14
  //   B: pin 10,9
  //   LD: pin 11
  //   LD0: pin 19
  //   LD1: pin 20
  //   LD2: pin 21
  //   LD3: pin 22
endmodule
